# Fritzing sketch LucesOBS (saved by Fritzing 0.9.9b)
breadboards: 1

parts:
  Relay_5V1 = Keyes Relay [package=THT]
  Relay_5V2 = Keyes Relay [package=THT]
  WeMos_D1_Mini1 = WeMos D1 Mini
  R1 = Resistor [tolerance=±5% power=0.25 resistance=330 package=THT]
  LED1 = LED - 5mm [color="Blue (505nm)" current=0.030 package="5 mm [THT]"]
  Relay_5V3 = Keyes Relay [package=THT]
  S1 = Pushbutton [package="[THT]"]

nets:
  N1: Relay_5V1.signal, Relay_5V2.signal, WeMos_D1_Mini1.5V, Relay_5V3.signal
  N2: Relay_5V1.power, WeMos_D1_Mini1.D1
  N3: Relay_5V1.ground, Relay_5V2.ground, WeMos_D1_Mini1.G, LED1.anode, Relay_5V3.ground, S1.Pin_1, S1.Pin_2
  N4: Relay_5V2.power, WeMos_D1_Mini1.D8
  N5: WeMos_D1_Mini1.D2, Relay_5V3.power
  N6: WeMos_D1_Mini1.D4, R1.Pin_1
  N7: WeMos_D1_Mini1.RST, S1.Pin_3, S1.Pin_4
  N8: R1.Pin_0, LED1.cathode

custom parts:
  Keyes Relay: The Keyes 5V relay module is suitable for SCM development, home appliance control. It uses a 5V~12V TIL control signal which can control DC / AC signal.

// code stored in the sketch: bluetoothLight.ino
char blueToothVal;           //value sent over via bluetooth
char lastValue;              //stores last state of device (on/off)
 
void setup()
{
 Serial.begin(9600); 
 pinMode(13,OUTPUT);
 pinMode(12,INPUT);
}
 
 
void loop()
{
  if(Serial.available())
  {//if there is data being recieved
    blueToothVal=Serial.read(); //read it
  }
  if (blueToothVal=='n')
  {//if value from bluetooth serial is n
    digitalWrite(13,HIGH);            //switch on LED
    if (lastValue!='n')
      Serial.println(F("LED is on")); //print LED is on
    lastValue=blueToothVal;
  }
  else if (blueToothVal=='f')
  {//if value from bluetooth serial is n
    digitalWrite(13,LOW);             //turn off LED
    if (lastValue!='f')
      Serial.println(F("LED is off")); //print LED is on
    lastValue=blueToothVal;
  }
  delay(250);
}
